# Fritzing sketch EsquemaConexiones (saved by Fritzing 0.9.3b)
breadboards: 1

parts:
  LED1 = LED - 5mm [color="Blue (430nm)" package="5 mm [THT]"]
  R1 = Resistor [tolerance=±5% resistance=330 package=THT]
  PIR1 = PIR sensor
  R2 = Resistor [tolerance=±5% resistance=330 package=THT]
  LED3 = LED - 5mm [color="Red (633nm)" package="5 mm [THT]"]
  R3 = Resistor [tolerance=±5% resistance=330 package=THT]
  Part1 = Arduino Uno (Rev3)
  LED2 = LED - 5mm [color="Yellow (595nm)" package="5 mm [THT]"]

nets:
  GND: LED1.cathode, PIR1.GND, LED3.cathode, Part1.GND, LED2.cathode
  N1: LED1.anode, R1.Pin_1
  N2: R1.Pin_0, Part1.D13/SCK
  VDD: PIR1.VDD, Part1.3V3
  N3: PIR1.SIG, Part1.D5_PWM
  N4: R2.Pin_0, Part1.D4
  N5: R2.Pin_1, LED2.anode
  N6: LED3.anode, R3.Pin_1
  N7: R3.Pin_0, Part1.D12/MISO
